// Logisim project trabalho de SD final (2º).circ as structural Verilog: 1 circuit, main circuit main
module main (
  input  A,
  input  B
);

  wire and_1_out, and_2_out, and_3_out, and_4_out, and_5_out, and_6_out, and_7_out, and_8_out, clock_1_out,
       d_ff_1_q, d_ff_1_qn, d_ff_2_q, d_ff_2_qn, not_1_out, not_2_out, or_1_out, or_2_out, xnor_1_out;

  Clock clock_1 (.out(clock_1_out));
  not not_1 (not_1_out, A);
  not not_2 (not_2_out, B);
  and and_1 (and_1_out, A, not_2_out);
  and and_2 (and_2_out, not_2_out, d_ff_1_q);
  and and_3 (and_3_out, A, d_ff_1_q);
  and and_4 (and_4_out, B, not_1_out);
  and and_5 (and_5_out, d_ff_2_q, not_1_out);
  and and_6 (and_6_out, d_ff_2_q, B);
  xnor xnor_1 (xnor_1_out, d_ff_1_q, d_ff_2_q);
  or or_1 (or_1_out, and_1_out, and_3_out, and_2_out);
  or or_2 (or_2_out, and_5_out, and_6_out, and_4_out);
  LED A_B (.in(xnor_1_out));
  D_Flip_Flop d_ff_1 (.clk(clock_1_out), .D(or_1_out), .Q(d_ff_1_q), .Qn(d_ff_1_qn));  // open: preset, en, reset
  LED A_B_2 (.in(and_7_out));
  and and_7 (and_7_out, d_ff_1_qn, d_ff_2_q);
  D_Flip_Flop d_ff_2 (.clk(clock_1_out), .D(or_2_out), .Q(d_ff_2_q), .Qn(d_ff_2_qn));  // open: preset, en, reset
  and and_8 (and_8_out, d_ff_1_q, d_ff_2_qn);
  LED A_B_3 (.in(and_8_out));
endmodule
