// Logisim project trabalhoSD.circ as structural Verilog: 1 circuit, main circuit main
module main (
  input  b,
  input  A1,
  input  A0,
  input  B1,
  input  B0
);

  wire A1_out, A_d_e_out, A_d_out, B1_out, C_2_out, C_3_out, C_4_out, c_5_out, C_out, e_2_out, e_3_out,
       e_4_out, e_out, f_2_out, f_out, not_1_out, not_2_out, not_3_out, not_4_out, or_1_out;

  not not_1 (not_1_out, A0);
  not not_2 (not_2_out, B0);
  not not_3 (not_3_out, A1);
  not not_4 (not_4_out, B1);
  and A_d_e (A_d_e_out, not_1_out, not_2_out);
  and C (C_out, B1, B0);
  and C_2 (C_2_out, A1, A0);
  and C_3 (C_3_out, not_3_out, not_4_out);
  not u_A1 (A1_out, A1);
  not u_B1 (B1_out, B1);
  or A_d (A_d_out, A1, A_d_e_out, B1);
  and e (e_out, A1, not_1_out, B1_out);
  and e_2 (e_2_out, B1, not_2_out, A1_out);
  or or_1 (or_1_out, A1, B1);
  and f (f_out, A1_out, not_1_out, B1_out);
  or C_4 (C_4_out, C_out, C_2_out);
  or c_5 (c_5_out, C_4_out, C_3_out);
  and f_2 (f_2_out, f_out, not_2_out);
  or e_3 (e_3_out, A_d_e_out, e_out);
  _7_Segment_Display u_7_segment_display_1 (
    .g(or_1_out), .f(f_2_out), .a(A_d_out), .b(b), .e(e_4_out), .d(A_d_out), .c(c_5_out));  // open: dp
  or e_4 (e_4_out, e_2_out, e_3_out);
endmodule
